// Logisim project ap2Contador.circ as structural Verilog
module main (
  input  RST,
  input  PULSO,
  output sf,
  output Saida_PULSO,
  output sg,
  output sa,
  output sb,
  output sc,
  output sd,
  output se
);

  wire n7447_1_pin3, not_1_out;
  wire [3:0] counter_1_q;

  not not_1 (not_1_out, RST);
  Counter #(.max('h9), .trigger("falling"), .width(4)) counter_1 (
    .clr(not_1_out), .load(1'b0), .up(1'b1), .count(1'b1), .clk(PULSO), .carry(Saida_PULSO), .Q(counter_1_q));  // open: D
  _7447 u_7447_1 (
    .pin1(counter_1_q[1]), .pin2(counter_1_q[2]), .pin3(n7447_1_pin3), .pin4(n7447_1_pin3),
    .pin5(n7447_1_pin3), .pin6(counter_1_q[3]), .pin7(counter_1_q[0]), .pin15(sf), .pin14(sg), .pin13(sa),
    .pin12(sb), .pin11(sc), .pin10(sd), .pin9(se));
  // also tied to VCC on the sheet: n7447_1_pin3
endmodule

module bloco (
  input  PIN_RST
);

  wire BLOCO1_sa, BLOCO1_saida_pulso, BLOCO1_sb, BLOCO1_sc, BLOCO1_sd, BLOCO1_se, BLOCO1_sf, BLOCO1_sg,
       BLOCO2_sa, BLOCO2_saida_pulso, BLOCO2_sb, BLOCO2_sc, BLOCO2_sd, BLOCO2_se, BLOCO2_sf, BLOCO2_sg,
       BLOCO3_sa, BLOCO3_saida_pulso, BLOCO3_sb, BLOCO3_sc, BLOCO3_sd, BLOCO3_se, BLOCO3_sf, BLOCO3_sg,
       BLOCO4_sa, BLOCO4_sb, BLOCO4_sc, BLOCO4_sd, BLOCO4_se, BLOCO4_sf, BLOCO4_sg, CLK_out;

  Clock CLK (.out(CLK_out));
  main BLOCO1 (
    .RST(PIN_RST), .PULSO(CLK_out), .sf(BLOCO1_sf), .Saida_PULSO(BLOCO1_saida_pulso), .sg(BLOCO1_sg),
    .sa(BLOCO1_sa), .sb(BLOCO1_sb), .sc(BLOCO1_sc), .sd(BLOCO1_sd), .se(BLOCO1_se));
  main BLOCO2 (
    .RST(PIN_RST), .PULSO(BLOCO1_saida_pulso), .sf(BLOCO2_sf), .Saida_PULSO(BLOCO2_saida_pulso),
    .sg(BLOCO2_sg), .sa(BLOCO2_sa), .sb(BLOCO2_sb), .sc(BLOCO2_sc), .sd(BLOCO2_sd), .se(BLOCO2_se));
  main BLOCO3 (
    .RST(PIN_RST), .PULSO(BLOCO2_saida_pulso), .sf(BLOCO3_sf), .Saida_PULSO(BLOCO3_saida_pulso),
    .sg(BLOCO3_sg), .sa(BLOCO3_sa), .sb(BLOCO3_sb), .sc(BLOCO3_sc), .sd(BLOCO3_sd), .se(BLOCO3_se));
  main BLOCO4 (
    .RST(PIN_RST), .PULSO(BLOCO3_saida_pulso), .sf(BLOCO4_sf), .sg(BLOCO4_sg), .sa(BLOCO4_sa),
    .sb(BLOCO4_sb), .sc(BLOCO4_sc), .sd(BLOCO4_sd), .se(BLOCO4_se));  // open: Saida_PULSO
  _7_Segment_Display #(.active("false")) UNIDADE (
    .g(BLOCO1_sg), .f(BLOCO1_sf), .a(BLOCO1_sa), .b(BLOCO1_sb), .e(BLOCO1_se), .d(BLOCO1_sd), .c(BLOCO1_sc),
    .dp(CLK_out));
  _7_Segment_Display #(.active("false")) DEZENA (
    .g(BLOCO2_sg), .f(BLOCO2_sf), .a(BLOCO2_sa), .b(BLOCO2_sb), .e(BLOCO2_se), .d(BLOCO2_sd), .c(BLOCO2_sc),
    .dp(1'b1));
  _7_Segment_Display #(.active("false")) CENTENA (
    .g(BLOCO3_sg), .f(BLOCO3_sf), .a(BLOCO3_sa), .b(BLOCO3_sb), .e(BLOCO3_se), .d(BLOCO3_sd), .c(BLOCO3_sc),
    .dp(1'b1));
  _7_Segment_Display #(.active("false")) MILHAR (
    .g(BLOCO4_sg), .f(BLOCO4_sf), .a(BLOCO4_sa), .b(BLOCO4_sb), .e(BLOCO4_se), .d(BLOCO4_sd), .c(BLOCO4_sc),
    .dp(1'b1));
endmodule

// VHDL entity count4, as the project stores it:
LIBRARY ieee;
USE ieee.std_logic_1164.all;
USE ieee.std_logic_unsigned.all;
ENTITY count4 IS
PORT (
clk : IN STD_LOGIC;
rst : IN STD_LOGIC;
q : OUT STD_LOGIC_VECTOR(3 DOWNTO 0);
carr : OUT STD_LOGIC
);
END ENTITY count4;
ARCHITECTURE trans OF count4 IS
SIGNAL count : STD_LOGIC_VECTOR(3 DOWNTO 0);
BEGIN
PROCESS (clk, rst)
BEGIN
IF (rst = '1') THEN
count <= "0000";
ELSE
IF (clk'EVENT AND clk = '1') THEN
IF (count ="1001") THEN
carr<='1';
ELSE
carr<='0';
END IF;
IF (count >= "1001") THEN
count <= "0000";
ELSE
count <= count + "0001";
END IF;
END IF;
END IF;
END PROCESS;
q <= count;
END ARCHITECTURE trans;

// VHDL entity bcd_7seg, as the project stores it:
LIBRARY ieee;
USE ieee.std_logic_1164.all;
ENTITY bcd_7seg IS
PORT (
entra : IN STD_LOGIC_VECTOR(3 DOWNTO 0);
sai : OUT STD_LOGIC_VECTOR(6 DownTO 0)
);
END bcd_7seg;
ARCHITECTURE trans OF bcd_7seg IS
BEGIN
PROCESS (entra)
BEGIN
CASE entra IS
WHEN "0000" =>
sai <= NOT("1111110");
WHEN "0001" =>
sai <= NOT("0110000");
WHEN "0010" =>
sai <= NOT("1101101");
WHEN "0011" =>
sai <= NOT("1111001");
WHEN "0100" =>
sai <= NOT("0110011");
WHEN "0101" =>
sai <= NOT("1011011");
WHEN "0110" =>
sai <= NOT("1011111");
WHEN "0111" =>
sai <= NOT("1110000");
WHEN "1000" =>
sai <= NOT("1111111");
WHEN "1001" =>
sai <= NOT("1111011");
WHEN OTHERS =>
sai <= NOT("0000000");
END CASE;
END PROCESS;

END trans;
