// Logisim project ap3.circ as structural Verilog
module main (
);

  wire count4_1_carr, count4_2_carr, count4_3_carr, count4_4_carr, count4_5_carr, PULSO, rst_out;
  wire [3:0] count4_1_q, count4_2_q, count4_3_q, count4_4_q, count4_5_q, count4_6_q;
  wire [6:0] bcd_7seg_1_sai, bcd_7seg_2_sai, bcd_7seg_3_sai, bcd_7seg_4_sai, bcd_7seg_5_sai, bcd_7seg_6_sai;

  Clock clock_1 (.out(PULSO));
  Button #(.press("passive")) rst (.out(rst_out));
  count4 count4_1 (.clk(PULSO), .rst(rst_out), .q(count4_1_q), .carr(count4_1_carr));
  count4 count4_2 (.clk(count4_1_carr), .rst(rst_out), .q(count4_2_q), .carr(count4_2_carr));
  count4 count4_3 (.clk(count4_2_carr), .rst(rst_out), .q(count4_3_q), .carr(count4_3_carr));
  count4 count4_4 (.clk(count4_3_carr), .rst(rst_out), .q(count4_4_q), .carr(count4_4_carr));
  count4 count4_5 (.clk(count4_4_carr), .rst(rst_out), .q(count4_5_q), .carr(count4_5_carr));
  count4 count4_6 (.clk(count4_5_carr), .rst(rst_out), .q(count4_6_q));  // open: carr
  bcd_7seg bcd_7seg_1 (.entra(count4_1_q), .sai(bcd_7seg_1_sai));
  bcd_7seg bcd_7seg_2 (.entra(count4_2_q), .sai(bcd_7seg_2_sai));
  bcd_7seg bcd_7seg_3 (.entra(count4_3_q), .sai(bcd_7seg_3_sai));
  bcd_7seg bcd_7seg_4 (.entra(count4_4_q), .sai(bcd_7seg_4_sai));
  bcd_7seg bcd_7seg_5 (.entra(count4_5_q), .sai(bcd_7seg_5_sai));
  bcd_7seg bcd_7seg_6 (.entra(count4_6_q), .sai(bcd_7seg_6_sai));
  _7_Segment_Display #(.active("false")) DISPLAY_U (
    .g(bcd_7seg_1_sai[0]), .f(bcd_7seg_1_sai[1]), .a(bcd_7seg_1_sai[6]), .b(bcd_7seg_1_sai[5]),
    .e(bcd_7seg_1_sai[2]), .d(bcd_7seg_1_sai[3]), .c(bcd_7seg_1_sai[4]), .dp(PULSO));
  _7_Segment_Display #(.active("false")) DISPLAY_D (
    .g(bcd_7seg_2_sai[0]), .f(bcd_7seg_2_sai[1]), .a(bcd_7seg_2_sai[6]), .b(bcd_7seg_2_sai[5]),
    .e(bcd_7seg_2_sai[2]), .d(bcd_7seg_2_sai[3]), .c(bcd_7seg_2_sai[4]), .dp(1'b1));
  _7_Segment_Display #(.active("false")) DISPLAY_C (
    .g(bcd_7seg_3_sai[0]), .f(bcd_7seg_3_sai[1]), .a(bcd_7seg_3_sai[6]), .b(bcd_7seg_3_sai[5]),
    .e(bcd_7seg_3_sai[2]), .d(bcd_7seg_3_sai[3]), .c(bcd_7seg_3_sai[4]), .dp(1'b1));
  _7_Segment_Display #(.active("false")) DISPLAY_M (
    .g(bcd_7seg_4_sai[0]), .f(bcd_7seg_4_sai[1]), .a(bcd_7seg_4_sai[6]), .b(bcd_7seg_4_sai[5]),
    .e(bcd_7seg_4_sai[2]), .d(bcd_7seg_4_sai[3]), .c(bcd_7seg_4_sai[4]), .dp(1'b1));
  _7_Segment_Display #(.active("false")) DISPLAY_M2 (
    .g(bcd_7seg_5_sai[0]), .f(bcd_7seg_5_sai[1]), .a(bcd_7seg_5_sai[6]), .b(bcd_7seg_5_sai[5]),
    .e(bcd_7seg_5_sai[2]), .d(bcd_7seg_5_sai[3]), .c(bcd_7seg_5_sai[4]), .dp(1'b1));
  _7_Segment_Display #(.active("false")) DISPLAY_M3 (
    .g(bcd_7seg_6_sai[0]), .f(bcd_7seg_6_sai[1]), .a(bcd_7seg_6_sai[6]), .b(bcd_7seg_6_sai[5]),
    .e(bcd_7seg_6_sai[2]), .d(bcd_7seg_6_sai[3]), .c(bcd_7seg_6_sai[4]), .dp(1'b1));
endmodule

// VHDL entity count4, as the project stores it:
LIBRARY ieee;
USE ieee.std_logic_1164.all;
USE ieee.std_logic_unsigned.all;
ENTITY count4 IS
PORT (
clk : IN STD_LOGIC;
rst : IN STD_LOGIC;
q : OUT STD_LOGIC_VECTOR(3 DOWNTO 0);
carr : OUT STD_LOGIC
);
END ENTITY count4;
ARCHITECTURE trans OF count4 IS
SIGNAL count : STD_LOGIC_VECTOR(3 DOWNTO 0);
BEGIN
PROCESS (clk, rst)
BEGIN
IF (rst = '1') THEN
count <= "0000";
ELSE
IF (clk'EVENT AND clk = '1') THEN
IF (count ="1001") THEN
carr<='1';
ELSE
carr<='0';
END IF;
IF (count >= "1001") THEN
count <= "0000";
ELSE
count <= count + "0001";
END IF;
END IF;
END IF;
END PROCESS;
q <= count;
END ARCHITECTURE trans;

// VHDL entity bcd_7seg, as the project stores it:
LIBRARY ieee;
USE ieee.std_logic_1164.all;
ENTITY bcd_7seg IS
PORT (
entra : IN STD_LOGIC_VECTOR(3 DOWNTO 0);
sai : OUT STD_LOGIC_VECTOR(6 DownTO 0)
);
END bcd_7seg;
ARCHITECTURE trans OF bcd_7seg IS
BEGIN
PROCESS (entra)
BEGIN
CASE entra IS
WHEN "0000" =>
sai <= NOT("1111110");
WHEN "0001" =>
sai <= NOT("0110000");
WHEN "0010" =>
sai <= NOT("1101101");
WHEN "0011" =>
sai <= NOT("1111001");
WHEN "0100" =>
sai <= NOT("0110011");
WHEN "0101" =>
sai <= NOT("1011011");
WHEN "0110" =>
sai <= NOT("1011111");
WHEN "0111" =>
sai <= NOT("1110000");
WHEN "1000" =>
sai <= NOT("1111111");
WHEN "1001" =>
sai <= NOT("1111011");
WHEN OTHERS =>
sai <= NOT("0000000");
END CASE;
END PROCESS;

END trans;
