// Logisim project mXor.circ as structural Verilog: 1 circuit, main circuit main
module main (
  input  Input_1,
  input  Input_2,
  output Output_1
);

  wire nand_1_out, nand_2_out, nand_3_out;

  nand nand_1 (nand_1_out, Input_1, Input_2);
  nand nand_2 (nand_2_out, Input_1, nand_1_out);
  nand nand_3 (nand_3_out, nand_1_out, Input_2);
  nand nand_4 (Output_1, nand_2_out, nand_3_out);
endmodule
