// Logisim project pg1.circ as structural Verilog: 1 circuit, main circuit main
module main (
);

  Counter #(.max('h9), .width(4)) counter_1 ();  // open: clr, load, up, count, clk, D, carry, Q
  _7447 u_7447_1 ();  // open: pin1, pin2, pin3, pin4, pin5, pin6, pin7, pin15, pin14, pin13, pin12, pin11, pin10, pin9
endmodule
